# Fritzing sketch diagram (saved by Fritzing 0.9.4)

parts:
  R1 = Rotary Potentiometer (Large) [maximum_resistance=100kΩ package=THT]
  U1 = POT [package=pot_mammoth]
  S2 = Toggle Switch [package=THT]
  Part2 = Arduino Pro Micro (Clone)
  S3 = Round Pushbutton

nets:
  N1: R1.leg1, U1.S, Part2.VCC
  N2: R1.wiper, Part2.A1
  N3: R1.leg2, U1.E, S2.COM, Part2.GND, S3.leg0
  N4: U1.A, Part2.A0
  N5: S2.L1, Part2.D7
  N6: S2.L2, Part2.D8
  N7: Part2.D9, S3.leg1
